# Fritzing sketch Multisensor_Sketch_wiring (saved by Fritzing 0.9.3b)

parts:
  U1 = NodeMCU V3.0
  Part1 = Adafruit TCA9548A
  LCD1 = LCD screen
  LCM1602_IIC2 = LCM1602 IIC [part_number="LCM1602 IIC" chip_label="LCM1602 IIC" package="DIP (Dual Inline) [THT]"]
  U2 = MLX90614 [package=to-39]
  U3 = MLX90614 [package=to-39]
  U4 = MLX90614 [package=to-39]

nets:
  N1: U1.D1, Part1.INPUTSCL, LCM1602_IIC2.SCL
  N2: U1.D2, Part1.INPUTSDA, LCM1602_IIC2.SDA
  GND: U1.GND, Part1.GND, LCM1602_IIC2.GND, U2.VSS, U3.VSS, U4.VSS
  VDD: U1.3V3, Part1.VCC, LCM1602_IIC2.VCC, U2.VDD, U3.VDD, U4.VDD
  N3: Part1.2SDA, U2.PWM_SDA
  N4: Part1.2SCL, U2.SCL_VZ
  N5: Part1.3SDA, U4.PWM_SDA
  N6: Part1.3SCL, U4.SCL_VZ
  N7: Part1.1SDA, U3.PWM_SDA
  N8: Part1.1SCL, U3.SCL_VZ
  VSS: LCD1.VSS, LCM1602_IIC2.VSS
  VDD_2: LCD1.VDD, LCM1602_IIC2.VDD
  N9: LCD1.V0, LCM1602_IIC2.V0
  N10: LCD1.RS, LCM1602_IIC2.RS
  N11: LCD1.R/W, LCM1602_IIC2.RW
  N12: LCD1.E, LCM1602_IIC2.E
  N13: LCD1.DB0, LCM1602_IIC2.D0
  N14: LCD1.DB1, LCM1602_IIC2.D1
  N15: LCD1.DB2, LCM1602_IIC2.D2
  N16: LCD1.DB3, LCM1602_IIC2.D3
  N17: LCD1.DB4, LCM1602_IIC2.D4
  N18: LCD1.DB5, LCM1602_IIC2.D5
  N19: LCD1.DB6, LCM1602_IIC2.D6
  N20: LCD1.DB7, LCM1602_IIC2.D7
  N21: LCD1.LED+, LCM1602_IIC2.A
  N22: LCD1.LED-, LCM1602_IIC2.K

custom parts:
  NodeMCU V3.0: NodeMcu V3 Lua WIFI Development Board
  Adafruit TCA9548A: You just found the perfect I2C sensor, and you want to wire up two or three or more of them to your Arduino when you realize "Uh oh, this chip has a fixed I2C address, and from what I know about I2C, you cannot have two devices with the same address on the same SDA/SCL pins!" Are you out of luck? You would be, if you didn't have this ultra-cool TCA9548A 1-to-8 I2C multiplexer! Finally, a way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
  LCM1602 IIC: I2C-Module to use a 1602 or 2004 LCD on with the wire.h libory Serial LCD Modul
